# Fritzing sketch Theodolite (saved by Fritzing 0.9.5d)

parts:
  U1 = POT [package=pot_mammoth]
  S1 = SWITCH-MOMENTARY-2 [package=tactile-pth-12mm]  # not connected
  S4 = Momentary Switch [package=ksa_sealed_tac_switch]
  Display1 = LCD screen 16x2 IIC [part_number=101290]
  Part1 = Arduino Uno (Rev3)
  J1 = Terminal Block - 3 pins [package=THT]

nets:
  VCC: U1.S, Display1.VCC, Part1.5V
  N1: U1.A, Part1.A0
  N2: U1.E, J1.Line_1
  N3: S4.2, J1.Line_2
  N4: S4.3, Part1.D8
  GND: Display1.GND, Part1.GND, J1.Line_3
  N5: Display1.SDA, Part1.A4/SDA
  N6: Display1.SCL, Part1.A5/SCL

custom parts:
  LCD screen 16x2 IIC: LCD screen with HD44780 controller enables showing text, symbols, value or anything else that comes from Croduino/Arduino. It is capable of showing 16 symbols in two lines and therefore can be used in many projects that need to send clearly visible and legible output information.. • Color of symbols: White • Backlight: Blue • Dimensions: 80 x 36 x 12 mm • Screen dimensions: 64.5 x 16 mm •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
  Terminal Block - 3 pins: Generic Screw Terminal 9.5mm
